# Fritzing sketch schema (saved by Fritzing 0.9.3b)
breadboards: 1

parts:
  Raspberry_Pi_B_rev2 = Raspberry Pi B rev2
  LCM1602_IIC2 = LCM1602 IIC [part_number="LCM1602 IIC" chip_label="LCM1602 IIC" package="DIP (Dual Inline) [THT]"]
  LCD2 = LCD screen
  LED1 = LED - 5mm [color="Red (633nm)" package="5 mm [THT]"]
  R1 = Resistor [tolerance=±5% resistance=220 package=THT]
  LED2 = LED - 5mm [color="Orange (605nm)" package="5 mm [THT]"]
  R2 = Resistor [tolerance=±5% resistance=220 package=THT]
  LED3 = LED - 5mm [color="Green (555nm)" package="5 mm [THT]"]
  R3 = Resistor [tolerance=±5% resistance=220 package=THT]
  J1 = Piezo Speaker
  S1 = Pushbutton [package="[THT]"]
  S2 = Pushbutton [package=THT]

nets:
  3V3: Raspberry_Pi_B_rev2.3V3, Raspberry_Pi_B_rev2.5V, LCM1602_IIC2.VCC
  GND: Raspberry_Pi_B_rev2.GIPO_2, Raspberry_Pi_B_rev2.GND, LCM1602_IIC2.GND, LCM1602_IIC2.SDA, LED1.anode, LED2.anode, LED3.anode, J1.pin1, S1.Pin_3, S1.Pin_4, S2.leg0
  N1: Raspberry_Pi_B_rev2.GIPO_3, LCM1602_IIC2.SCL
  N2: Raspberry_Pi_B_rev2.GPIO_23, R2.Pin_0
  N3: Raspberry_Pi_B_rev2.GPIO_22, R1.Pin_0
  N4: Raspberry_Pi_B_rev2.GPIO_24, R3.Pin_0
  N5: Raspberry_Pi_B_rev2.GPIO_9, S2.leg1
  N6: Raspberry_Pi_B_rev2.GPIO_25, S1.Pin_1, S1.Pin_2
  VSS: LCM1602_IIC2.VSS, LCD2.VSS
  VDD: LCM1602_IIC2.VDD, LCD2.VDD
  N7: LCM1602_IIC2.V0, LCD2.V0
  N8: LCM1602_IIC2.RS, LCD2.RS
  N9: LCM1602_IIC2.RW, LCD2.R/W
  N10: LCM1602_IIC2.E, LCD2.E
  N11: LCM1602_IIC2.D0, LCD2.DB0
  N12: LCM1602_IIC2.D1, LCD2.DB1
  N13: LCM1602_IIC2.D2, LCD2.DB2
  N14: LCM1602_IIC2.D3, LCD2.DB3
  N15: LCM1602_IIC2.D4, LCD2.DB4
  N16: LCM1602_IIC2.D5, LCD2.DB5
  N17: LCM1602_IIC2.D6, LCD2.DB6
  N18: LCM1602_IIC2.D7, LCD2.DB7
  N19: LCM1602_IIC2.A, LCD2.LED+
  N20: LCM1602_IIC2.K, LCD2.LED-
  N21: LED1.cathode, R1.Pin_1
  N22: LED2.cathode, R2.Pin_1
  N23: LED3.cathode, R3.Pin_1

custom parts:
  LCM1602 IIC: I2C-Module to use a 1602 or 2004 LCD on with the wire.h libory Serial LCD Modul
